// Logisim project Cache.circ as structural Verilog: 10 circuits, main circuit main
module main (
  input  EnableTestHalting,
  output [9:0] CorrectCounter,
  output [9:0] HitCounter,
  output [9:0] MissCounter,
  output [9:0] TestNumber,
  output [7:0] ByteRead,
  output [7:0] CorrectByteRead,
  output Halt
);

  wire and_3_out, and_4_out, and_5_out, CLK, CmdIsRead, Correct, CpuRead, CpuWrite, DidContain, HaltTesting,
       MaxItersReached, MemRead, MemWrite, not_1_out, not_2_out, not_4_out, NotDoneTesting, Ok2Count,
       or_1_out, Ready;
  wire [7:0] CpuWriteValue, MemAddress;
  wire [9:0] CpuAddress;
  wire [31:0] Line2Mem, LineFromMem;

  not not_1 (not_1_out, Ready);
  Clock clock_1 (.out(CLK));
  or or_1 (or_1_out, MaxItersReached, Ready);
  Counter #(.width(4), .max('h9)) MaxClocks (
    .load(Ready), .D(4'b0001), .count(not_1_out), .carry(MaxItersReached), .clk(CLK));  // open: Q, clr
  and and_1 (HaltTesting, EnableTestHalting, CmdIsRead, not_2_out);
  not not_2 (not_2_out, Correct);
  not not_3 (NotDoneTesting, Halt);
  Inputs inputs_1 (
    .HaltTesting(HaltTesting), .Ready(or_1_out), .CLK(CLK), .Done(Halt), .Read(CpuRead), .Write(CpuWrite),
    .Address(CpuAddress), .Value(CpuWriteValue), .TestNumber(TestNumber));
  Cache cache_1 (
    .CpuAddress(CpuAddress), .CpuRead(CpuRead), .CpuWrite(CpuWrite), .CpuWriteValue(CpuWriteValue),
    .CLK(CLK), .Ready(Ready), .DidContain(DidContain), .ByteRead(ByteRead), .MemAddress(MemAddress),
    .MemRead(MemRead), .MemWrite(MemWrite), .LineFromMem(LineFromMem), .Line2Mem(Line2Mem));
  // Probe on CpuRead
  // Probe on CpuWrite
  // Probe on CpuAddress
  // Probe on CpuWriteValue
  // Probe on TestNumber
  // Probe on CorrectByteRead
  // Probe on Correct
  // Probe on Ready
  // Probe on DidContain
  // Probe on ByteRead
  // Probe on MemAddress
  // Probe on MemRead
  // Probe on MemWrite
  // Probe on HitCounter
  // Probe on LineFromMem
  // Probe on Line2Mem
  not not_4 (not_4_out, HaltTesting);
  RAM #(.dataWidth(32), .bus("separate")) ram_1 (
    .addr(MemAddress), .din(Line2Mem), .data(LineFromMem), .str(MemWrite), .clk(CLK), .ld(MemRead));  // open: sel, clr
  and and_2 (Ok2Count, Ready, not_4_out, NotDoneTesting);
  and and_3 (and_3_out, Correct, Ok2Count);
  and and_4 (and_4_out, DidContain, Ok2Count);
  and and_5 (and_5_out, MemRead, NotDoneTesting);
  Checker checker_1 (
    .TestNumber(TestNumber), .YourByteRead(ByteRead), .CmdIsRead(CmdIsRead),
    .CorrectByteRead(CorrectByteRead), .Correct(Correct));
  Counter #(.width(10), .max('h3ff)) u_CorrectCounter (
    .count(and_3_out), .Q(CorrectCounter), .clk(CLK));  // open: load, D, carry, clr
  Counter #(.width(10), .max('h3ff)) u_HitCounter (
    .count(and_4_out), .Q(HitCounter), .clk(CLK));  // open: load, D, carry, clr
  Counter #(.width(10), .max('h3ff)) u_MissCounter (
    .count(and_5_out), .Q(MissCounter), .clk(CLK));  // open: load, D, carry, clr
  // Probe on CorrectCounter
  // Probe on HitCounter
  // Probe on MissCounter

  // Other names for the same wires on the sheet: DoneTesting = Halt

  // Notes on the sheet:
  //   Your Answer Inside Here
endmodule

module Cache (
  input  [9:0] CpuAddress,
  input  CpuRead,
  input  CpuWrite,
  input  [7:0] CpuWriteValue,
  input  CLK,
  input  [31:0] LineFromMem,
  output Ready,
  output DidContain,
  output [7:0] ByteRead,
  output [7:0] MemAddress,
  output MemRead,
  output MemWrite,
  output [31:0] Line2Mem
);

  wire CacheContains, ReadFromSet0, ReadFromSet1, Set1Contains, WriteToSet0, WriteToSet1;
  wire [1:0] OffsetToSet0, OffsetToSet1;
  wire [6:0] TagToSet0, TagToSet1;
  wire [7:0] Set0Contains;
  wire [31:0] MemToSet0, MemToSet1;

  Demultiplexer #(.width(7), .enable("false")) demultiplexer_1 (
    .out0(TagToSet0), .out1(TagToSet1), .in(CpuAddress[9:3]), .sel(CpuAddress[2]));
  Demultiplexer #(.width(2), .enable("false")) demultiplexer_2 (
    .out0(OffsetToSet0), .out1(OffsetToSet1), .in(CpuAddress[1:0]), .sel(CpuAddress[2]));
  Demultiplexer #(.enable("false")) demultiplexer_3 (
    .out0(ReadFromSet0), .out1(ReadFromSet1), .in(CpuRead), .sel(CpuAddress[2]));
  Demultiplexer #(.enable("false")) demultiplexer_4 (
    .out0(WriteToSet0), .out1(WriteToSet1), .in(CpuWrite), .sel(CpuAddress[2]));
  Demultiplexer #(.width(32), .enable("false")) demultiplexer_5 (
    .out0(MemToSet0), .out1(MemToSet1), .in(LineFromMem), .sel(CpuAddress[2]));
  Set set_1 (
    .CLK(CLK), .Read(ReadFromSet0), .Write(WriteToSet0), .LineFromMem(MemToSet0), .Tag(TagToSet0),
    .Offset(OffsetToSet0), .ByteRead(Set0Contains));  // open: Contains, Dirty, StoredTag, Line2Mem
  Set Set1 (
    .CLK(CLK), .Read(ReadFromSet1), .Write(WriteToSet1), .LineFromMem(MemToSet1), .Tag(TagToSet1),
    .Offset(OffsetToSet1), .Contains(Set1Contains));  // open: Dirty, ByteRead, StoredTag, Line2Mem
  Multiplexer #(.enable("false")) multiplexer_1 (
    .in0(Set0Contains[0]), .in1(Set1Contains), .out(CacheContains), .sel(CpuAddress[2]));
  // Pins of 1 and 8 bits meet at Set0Contains

  // Other names for the same wires on the sheet: Set = CpuAddress[2]; Offset[1:0] = CpuAddress[1:0];
  //   Tag[6:0] = CpuAddress[9:3]

  // Notes on the sheet:
  //   Address Bits = 10
  //   (1) Split CPU Address
  //   Line Size = 4
  //   Get coordinates to look inside cache
  //   W = 3
  //   (2) Using Set: feed the Offset, Tag, CpuRead, and CpuWrite to the right set
  //   Num Sets = 2
  //   C =4*3*2 = 24bytes
  //   Tag bits = 7
endmodule

module Inputs (
  input  HaltTesting,
  input  Ready,
  input  CLK,
  output Done,
  output Read,
  output Write,
  output [9:0] Address,
  output [7:0] Value,
  output [9:0] TestNumber
);

  wire and_1_out, not_1_out, not_2_out;

  not not_1 (not_1_out, HaltTesting);
  not not_2 (not_2_out, Done);
  Counter #(.width(10), .max('h3ff), .ongoal("stay")) u_TestNumber (
    .count(and_1_out), .Q(TestNumber), .clk(CLK));  // open: load, D, carry, clr
  and and_1 (and_1_out, not_1_out, Ready, not_2_out);
  ROM #(.addrWidth(10), .dataWidth(21)) rom_1 (
    .addr(TestNumber), .data({Done, Read, Write, Address, Value}));  // open: sel

  // Notes on the sheet:
  //   contents of rom_1 (hex, n*v repeats v):
  //   40005 40106 40307 40308 41009 4110a 4130b 4130c 4200d 4210e 4230f 42310 43011 43112 43313 43314
  //   44015 44116 44317 44318 45019 4511a 4531b 4531c 80000 80100 80300 80300 81000 81100 81300 81300
  //   82000 82100 82300 82300 83000 83100 83300 83300 84000 84100 84300 84300 85000 85100 85300 85300 0
  //   100000
endmodule

module Checker (
  input  [9:0] TestNumber,
  input  [7:0] YourByteRead,
  output CmdIsRead,
  output [7:0] CorrectByteRead,
  output Correct
);

  wire comparator_1_eq;
  wire [9:0] subtractor_1_out;

  // Probe on TestNumber
  Subtractor #(.width(10)) subtractor_1 (.a(TestNumber), .b(10'h1), .out(subtractor_1_out));  // open: bin, bout
  ROM #(.addrWidth(10), .dataWidth(9)) rom_1 (
    .addr(subtractor_1_out), .data({CmdIsRead, CorrectByteRead}));  // open: sel
  Comparator #(.mode("unsigned")) comparator_1 (
    .a(YourByteRead), .b(CorrectByteRead), .eq(comparator_1_eq));  // open: gt, lt
  and and_1 (Correct, comparator_1_eq, CmdIsRead);

  // Other names for the same wires on the sheet: Test_Number[9:0] = TestNumber

  // Notes on the sheet:
  //   Read Solutions
  //   contents of rom_1 (hex, n*v repeats v):
  //   5 6 7 8 9 a b c d e f 10 11 12 13 14 15 16 17 18 19 1a 1b 1c 105 106 108 108 109 10a 10c 10c 10d 10e
  //   110 110 111 112 114 114 115 116 118 118 119 11a 11c 11c
endmodule

module Line (
  input  [6:0] TagIn,
  input  UpdateTag,
  input  DirtyBitIn,
  input  UpdateDirtyBit,
  input  ValidIn,
  input  UpdateValid,
  input  [1:0] AgeIn,
  input  UpdateAge,
  input  [1:0] Offset,
  input  CLK,
  input  [7:0] Val0In,
  input  [7:0] Val1In,
  input  [7:0] Val2In,
  input  [7:0] Val3In,
  input  WriteToVal,
  output [6:0] TagOut,
  output DirtyBitOut,
  output ValidOut,
  output [1:0] AgeOut,
  output [7:0] ValueOut,
  output ContainsTag,
  output [31:0] Line2Mem
);

  Register #(.width(7)) register_1 (.D(TagIn), .en(UpdateTag), .Q(TagOut), .clk(CLK));  // open: clr
  Register #(.width(1)) register_2 (.D(DirtyBitIn), .en(UpdateDirtyBit), .Q(DirtyBitOut), .clk(CLK));  // open: clr
  Register #(.width(1)) register_3 (.D(ValidIn), .en(UpdateValid), .Q(ValidOut), .clk(CLK));  // open: clr
  Register #(.width(2)) register_4 (.D(AgeIn), .en(UpdateAge), .Q(AgeOut), .clk(CLK));  // open: clr
  Register Val0 (.D(Val0In), .en(WriteToVal), .Q(Line2Mem[7:0]), .clk(CLK));  // open: clr
  Register Val1 (.D(Val1In), .en(WriteToVal), .Q(Line2Mem[15:8]), .clk(CLK));  // open: clr
  Register Val2 (.D(Val2In), .en(WriteToVal), .Q(Line2Mem[23:16]), .clk(CLK));  // open: clr
  Register Val3 (.D(Val3In), .en(WriteToVal), .Q(Line2Mem[31:24]), .clk(CLK));  // open: clr
  // Probe on Line2Mem[31:24]
  Comparator #(.width(7), .mode("unsigned")) comparator_1 (.a(TagIn), .b(TagOut), .eq(ContainsTag));  // open: gt, lt
  Multiplexer #(.select(2), .width(8), .enable("false")) multiplexer_1 (
    .in0(Line2Mem[7:0]), .in1(Line2Mem[15:8]), .in2(Line2Mem[23:16]), .in3(Line2Mem[31:24]), .out(ValueOut),
    .sel(Offset));

  // Other names for the same wires on the sheet: Val0Out[7:0] = Line2Mem[7:0]; Val1Out[7:0] = Line2Mem[15:8];
  //   Val2Out[7:0] = Line2Mem[23:16]; Val3Out[7:0] = Line2Mem[31:24]

  // Notes on the sheet:
  //   Line returns currently stored Tag, Dirty Bit, Valid, and Age Data
  //   Based on Offset, return the correct Value
endmodule

module nextAge (
  input  Set,
  input  Set_2
);

  Multiplexer #(.select(2), .width(7), .enable("false")) multiplexer_1 ();  // open: in0, in1, in2, in3, out, sel
endmodule

module Set (
  input  CLK,
  input  Read,
  input  Write,
  input  [31:0] LineFromMem,
  input  [6:0] Tag,
  input  [1:0] Offset,
  output Contains,
  output Dirty,
  output [7:0] ByteRead,
  output [6:0] StoredTag,
  output [31:0] Line2Mem
);

  wire ContainsTagLine0, ContainsTagLine1, DirtyBitLine0, DirtyBitLine1, DirtyBitLine2, DirtyBitToLine0,
       DirtyBitToLine1, DirtyBitToLine2, UpdateAgeLine0, UpdateAgeLine1, UpdateAgeLine2, UpdateDirtyBitLine0,
       UpdateDirtyBitLine1, UpdateDirtyBitLine2, UpdateTagLine0, UpdateTagLine1, UpdateTagLine2,
       UpdateValidLine0, UpdateValidLine1, UpdateValidLine2, ValidLine0, ValidLine1, ValidLine2,
       ValidToLine0, ValidToLine1, ValidToLine2, WriteToValLine0, WriteToValLine1, WriteToValLine2;
  wire [1:0] AgeLine0, AgeLine1, AgeLine2, OffsetToLine0, OffsetToLine1, OffsetToLine2;
  wire [6:0] Tag0, Tag1, Tag2, TagLine0, TagLine1, TagLine2, TagToLine0, TagToLine1, TagToLine2;
  wire [7:0] Val0ToLine0, Val0ToLine1, Val0ToLine2, Val1ToLine0, Val1ToLine1, Val1ToLine2, Val2ToLine0,
       Val2ToLine1, Val2ToLine2, Val3ToLine0, Val3ToLine1, Val3ToLine2, ValLine0, ValLine1, ValLine2;
  wire [31:0] Line02Mem, Line12Mem, Line22Mem;

  Demultiplexer #(.select(2), .width(7), .enable("false")) demultiplexer_1 (
    .out0(TagToLine0), .out1(TagToLine1), .out2(TagToLine2), .in(Tag), .sel(2'b00));  // open: out3
  Demultiplexer #(.select(2), .width(2), .enable("false")) demultiplexer_2 (
    .out0(OffsetToLine0), .out1(OffsetToLine1), .out2(OffsetToLine2), .in(Offset), .sel(2'b00));  // open: out3
  Demultiplexer #(.select(2), .enable("false")) demultiplexer_3 (
    .out0(UpdateTagLine0), .out1(UpdateTagLine1), .out2(UpdateTagLine2), .in(1'b0), .sel(2'b00));  // open: out3
  Demultiplexer #(.select(2), .enable("false")) demultiplexer_4 (
    .out0(DirtyBitToLine0), .out1(DirtyBitToLine1), .out2(DirtyBitToLine2), .in(1'b0), .sel(2'b00));  // open: out3
  Demultiplexer #(.select(2), .enable("false")) demultiplexer_5 (
    .out0(UpdateDirtyBitLine0), .out1(UpdateDirtyBitLine1), .out2(UpdateDirtyBitLine2), .in(1'b0), .sel(2'b00));  // open: out3
  Demultiplexer #(.select(2), .enable("false")) demultiplexer_6 (
    .out0(ValidToLine0), .out1(ValidToLine1), .out2(ValidToLine2), .in(1'b0), .sel(2'b00));  // open: out3
  Demultiplexer #(.select(2), .enable("false")) demultiplexer_7 (
    .out0(UpdateValidLine0), .out1(UpdateValidLine1), .out2(UpdateValidLine2), .in(1'b0), .sel(2'b00));  // open: out3
  UpdateAge updateage_1 ();  // open: currentAge, ageAccessed, nextAge
  Demultiplexer #(.select(2), .enable("false")) demultiplexer_8 (
    .out0(UpdateAgeLine0), .out1(UpdateAgeLine1), .out2(UpdateAgeLine2), .in(1'b0), .sel(2'b00));  // open: out3
  Demultiplexer #(.select(2), .width(8), .enable("false")) demultiplexer_9 (
    .out0(Val0ToLine0), .out1(Val0ToLine1), .out2(Val0ToLine2), .in(LineFromMem[31:24]), .sel(2'b00));  // open: out3
  Demultiplexer #(.select(2), .width(8), .enable("false")) demultiplexer_10 (
    .out0(Val1ToLine0), .out1(Val1ToLine1), .out2(Val1ToLine2), .in(LineFromMem[23:16]), .sel(2'b00));  // open: out3
  Demultiplexer #(.select(2), .width(8), .enable("false")) demultiplexer_11 (
    .out0(Val2ToLine0), .out1(Val2ToLine1), .out2(Val2ToLine2), .in(LineFromMem[15:8]), .sel(2'b00));  // open: out3
  Demultiplexer #(.select(2), .width(8), .enable("false")) demultiplexer_12 (
    .out0(Val3ToLine0), .out1(Val3ToLine1), .out2(Val3ToLine2), .in(LineFromMem[7:0]), .sel(2'b00));  // open: out3
  Demultiplexer #(.select(2), .enable("false")) demultiplexer_13 (
    .out0(WriteToValLine0), .out1(WriteToValLine1), .out2(WriteToValLine2), .in(Write), .sel(2'b00));  // open: out3
  Line Line0 (
    .TagIn(TagToLine0), .UpdateTag(UpdateTagLine0), .DirtyBitIn(DirtyBitToLine0),
    .UpdateDirtyBit(UpdateDirtyBitLine0), .ValidIn(ValidToLine0), .UpdateValid(UpdateValidLine0),
    .UpdateAge(UpdateAgeLine0), .Offset(OffsetToLine0), .CLK(CLK), .Val0In(Val0ToLine0),
    .Val1In(Val1ToLine0), .Val2In(Val2ToLine0), .Val3In(Val3ToLine0), .WriteToVal(WriteToValLine0),
    .TagOut(TagLine0), .DirtyBitOut(DirtyBitLine0), .ValidOut(ValidLine0), .AgeOut(AgeLine0),
    .ValueOut(ValLine0), .ContainsTag(ContainsTagLine0), .Line2Mem(Line02Mem));  // open: AgeIn
  Line Line1 (
    .TagIn(TagToLine1), .UpdateTag(UpdateTagLine1), .DirtyBitIn(DirtyBitToLine1),
    .UpdateDirtyBit(UpdateDirtyBitLine1), .ValidIn(ValidToLine1), .UpdateValid(UpdateValidLine1),
    .UpdateAge(UpdateAgeLine1), .Offset(OffsetToLine1), .CLK(CLK), .Val0In(Val0ToLine1),
    .Val1In(Val1ToLine1), .Val2In(Val2ToLine1), .Val3In(Val3ToLine1), .WriteToVal(WriteToValLine1),
    .TagOut(TagLine1), .DirtyBitOut(DirtyBitLine1), .ValidOut(ValidLine1), .AgeOut(AgeLine1),
    .ValueOut(ValLine1), .ContainsTag(ContainsTagLine1), .Line2Mem(Line12Mem));  // open: AgeIn
  Line Line2 (
    .TagIn(TagToLine2), .UpdateTag(UpdateTagLine2), .DirtyBitIn(DirtyBitToLine2),
    .UpdateDirtyBit(UpdateDirtyBitLine2), .ValidIn(ValidToLine2), .UpdateValid(UpdateValidLine2),
    .UpdateAge(UpdateAgeLine2), .Offset(OffsetToLine2), .CLK(CLK), .Val0In(Val0ToLine2),
    .Val1In(Val1ToLine2), .Val2In(Val2ToLine2), .Val3In(Val3ToLine2), .WriteToVal(WriteToValLine2),
    .TagOut(TagLine2), .DirtyBitOut(DirtyBitLine2), .ValidOut(ValidLine2), .AgeOut(AgeLine2),
    .ValueOut(ValLine2), .ContainsTag(ContainsTagLine1), .Line2Mem(Line22Mem));  // open: AgeIn
  Multiplexer #(.select(2), .width(8), .enable("false")) multiplexer_1 (
    .in0(ValLine0), .in1(ValLine1), .in2(ValLine2), .out(ByteRead), .sel(2'b00));  // open: in3
  Multiplexer #(.select(2), .width(7), .enable("false")) multiplexer_2 (
    .in0(Tag0), .in1(Tag1), .in2(Tag2), .out(StoredTag), .sel(2'b00));  // open: in3
  Multiplexer #(.select(2), .width(32), .enable("false")) multiplexer_3 (
    .in0(Line02Mem), .in1(Line12Mem), .in2(Line22Mem), .out(Line2Mem), .sel(2'b00));  // open: in3
  // AND_Gate and_1 has open pins: in0=ContainsTagLine0, in1=ValidLine0, out=open
  // AND_Gate and_2 has open pins: in0=ContainsTagLine1, in1=ValidLine0, out=open
  // AND_Gate and_3 has open pins: in0=ContainsTagLine0, in1=ValidLine0, out=open

  // Other names for the same wires on the sheet: Val3[7:0] = LineFromMem[7:0]; Val2[7:0] = LineFromMem[15:8];
  //   Val1[7:0] = LineFromMem[23:16]; Val0[7:0] = LineFromMem[31:24]; WriteToVal = Write

  // Notes on the sheet:
  //   Update Age After Block has been evicted and written
  //   FSM Outputs/Inputs
  //   FSN output
endmodule

module Test (
  input  [6:0] UpdateTag,
  input  UpdateTag_2,
  input  DirtyBitIn,
  input  UpdateDirtyBit,
  input  ValidIn,
  input  UpdateValid,
  input  [1:0] Age,
  input  UpdateAge,
  input  [1:0] Offset,
  input  [7:0] Val0In,
  input  [7:0] Val1In,
  input  [7:0] Val2In,
  input  [7:0] Val3In,
  input  WriteToVal,
  output [6:0] Tag,
  output DirtyBit,
  output Valid,
  output [1:0] Age_2,
  output [7:0] Val,
  output ContainsTag
);

  wire clock_1_out;

  Clock clock_1 (.out(clock_1_out));
  Line line_1 (
    .TagIn(UpdateTag), .UpdateTag(UpdateTag_2), .DirtyBitIn(DirtyBitIn), .UpdateDirtyBit(UpdateDirtyBit),
    .ValidIn(ValidIn), .UpdateValid(UpdateValid), .AgeIn(Age), .UpdateAge(UpdateAge), .Offset(Offset),
    .CLK(clock_1_out), .Val0In(Val0In), .Val1In(Val1In), .Val2In(Val2In), .Val3In(Val3In),
    .WriteToVal(WriteToVal), .TagOut(Tag), .DirtyBitOut(DirtyBit), .ValidOut(Valid), .AgeOut(Age_2),
    .ValueOut(Val), .ContainsTag(ContainsTag));  // open: Line2Mem
endmodule

module UpdateAge (
  input  [1:0] currentAge,
  input  [1:0] ageAccessed,
  output [1:0] nextAge
);

  wire equal, greater, less;
  wire [1:0] adder_1_out, flag;

  Adder #(.width(2)) adder_1 (.a(currentAge), .b(2'b01), .out(adder_1_out));  // open: cin, cout
  Comparator #(.width(2), .mode("unsigned")) comparator_1 (
    .a(currentAge), .b(ageAccessed), .gt(greater), .eq(equal), .lt(less));
  Multiplexer #(.select(2), .width(2), .enable("false")) multiplexer_1 (
    .in0(2'b00), .in1(currentAge), .in2(adder_1_out), .out(nextAge), .sel(flag));  // open: in3
  comparationConverter comparationconverter_1 (
    .greater(greater), .equal(equal), .less(less), .flag1(flag[1]), .flag0(flag[0]));
  // Probe on flag
endmodule

module comparationConverter (
  input  greater,
  input  equal,
  input  less,
  output flag1,
  output flag0
);


  assign flag0 = greater;
  assign flag1 = less;
endmodule
